// Logisim project ALU.circ as structural Verilog: 1 circuit, main circuit main
module main (
  input  [31:0] dataA,
  input  [31:0] dataB,
  input  [3:0] sel,
  output [31:0] dataD
);

  wire comparator_1_lt, comparator_2_lt;
  wire [31:0] addOut, andOut, orOut, sllOut, sltOut, sltuOut, sraOut, srlOut, subOut, xorOut;

  assign orOut = dataA | dataB;  // OR_Gate or_1, 32 bits wide
  assign andOut = dataA & dataB;  // AND_Gate and_1, 32 bits wide
  Adder #(.width(32)) adder_1 (.a(dataA), .b(dataB), .out(addOut));  // open: cin, cout
  Subtractor #(.width(32)) subtractor_1 (.a(dataA), .b(dataB), .out(subOut));  // open: bin, bout
  Shifter #(.width(32)) shifter_1 (.in(dataA), .\dist (dataB[4:0]), .out(sllOut));
  Comparator #(.width(32)) comparator_1 (.a(dataA), .b(dataB), .lt(comparator_1_lt));  // open: gt, eq
  assign sltOut = {{31{1'b0}}, comparator_1_lt};  // Bit_Extender bit_extender_1
  Comparator #(.mode("unsigned"), .width(32)) comparator_2 (
    .a(dataA), .b(dataB), .lt(comparator_2_lt));  // open: gt, eq
  assign sltuOut = {{31{1'b0}}, comparator_2_lt};  // Bit_Extender bit_extender_2
  assign xorOut = dataA ^ dataB;  // XOR_Gate xor_1, 32 bits wide
  Shifter #(.shift("lr"), .width(32)) shifter_2 (.in(dataA), .\dist (dataB[4:0]), .out(srlOut));
  Shifter #(.shift("ar"), .width(32)) shifter_3 (.in(dataA), .\dist (dataB[4:0]), .out(sraOut));
  Multiplexer #(.select(4), .width(32)) multiplexer_1 (
    .in0(addOut), .in1(sllOut), .in2(sltOut), .in3(sltuOut), .in4(xorOut), .in5(srlOut), .in6(orOut),
    .in7(addOut), .in8(subOut), .in13(sraOut), .out(dataD), .sel(sel));  // open: in9, in10, in11, in12, in14, in15

  // Other names for the same wires on the sheet: dataA_t[31:0] = dataA; dataB_t[31:0] = dataB;
  //   dataBL5_t[4:0] = dataB[4:0]; dataD_t[31:0] = dataD; sel_t[3:0] = sel
endmodule
