// Logisim project Brancher.circ as structural Verilog: 1 circuit, main circuit main
module main (
  input  [31:0] dataA,
  input  [31:0] dataB,
  input  brUn,
  output brLt,
  output beEq
);

  wire comparator_1_lt, comparator_2_lt;

  Comparator #(.width(32)) comparator_1 (.a(dataA), .b(dataB), .eq(beEq), .lt(comparator_1_lt));  // open: gt
  Comparator #(.mode("unsigned"), .width(32)) comparator_2 (
    .a(dataA), .b(dataB), .lt(comparator_2_lt));  // open: gt, eq
  Multiplexer multiplexer_1 (.in0(comparator_1_lt), .in1(comparator_2_lt), .out(brLt), .sel(brUn));

  // Other names for the same wires on the sheet: brEq_t = beEq; brLt_t = brLt; brUn_t = brUn; dataA_t[31:0] = dataA;
  //   dataB_t[31:0] = dataB
endmodule
