// Logisim project FinalRISEX.circ as structural Verilog: 16 circuits, main circuit immediateGenerator
module datapath (
  output [31:0] out_1
);

  wire bsel_t, clock_1_out, controllogic_1_regwena;
  wire [2:0] immsel_t;
  wire [3:0] controllogic_1_alusel;
  wire [31:0] aluctl_1_datab, immediategenerator_1_imm31_0, registerfile_1_rs1, registerfile_1_rs2;

  Clock clock_1 (.out(clock_1_out));
  RegisterFile registerfile_1 (
    .rsi1(5'b00011), .rsi2(5'b00100), .rdi(5'b00010), .rd(out_1), .we(controllogic_1_regwena),
    .clk(clock_1_out), .rs1(registerfile_1_rs1), .rs2(registerfile_1_rs2));
  immediateGenerator immediategenerator_1 (.ins(32'h418133), .sel(immsel_t), .imm31_0(immediategenerator_1_imm31_0));
  ALUctl aluctl_1 (
    .rs2(registerfile_1_rs2), .imm31_0(immediategenerator_1_imm31_0), .bsel(bsel_t), .dataB(aluctl_1_datab));
  ControlLogic controllogic_1 (
    .ins(32'h418133), .alusel(controllogic_1_alusel), .regwena(controllogic_1_regwena), .immsel(immsel_t),
    .bsel(bsel_t));
  RAM #(.dataWidth(32)) ram_1 ();  // open: addr, we, oe, clk, din, dout
  Alu alu_1 (.dataA(registerfile_1_rs1), .dataB(aluctl_1_datab), .sel(controllogic_1_alusel), .dataD(out_1));

  // Notes on the sheet:
  //   add,x2,x3,x4
  //   sub,x2,x3,x4
  //   or,x2,x3,x4
  //   add,x2,x3,x4
endmodule

module Alu (
  input  [31:0] dataA,
  input  [31:0] dataB,
  input  [3:0] sel,
  output [31:0] dataD
);

  wire comparator_1_lt, comparator_2_lt;
  wire [31:0] addOut, andOut, orOut, sllOut, sltOut, sltuOut, sraOut, srlOut, subOut, xorOut;

  assign orOut = dataA | dataB;  // OR_Gate or_1, 32 bits wide
  assign andOut = dataA & dataB;  // AND_Gate and_1, 32 bits wide
  Adder #(.width(32)) adder_1 (.a(dataA), .b(dataB), .out(addOut));  // open: cin, cout
  Subtractor #(.width(32)) subtractor_1 (.a(dataA), .b(dataB), .out(subOut));  // open: bin, bout
  Shifter #(.width(32)) shifter_1 (.in(dataA), .\dist (dataB[4:0]), .out(sllOut));
  Comparator #(.width(32)) comparator_1 (.a(dataA), .b(dataB), .lt(comparator_1_lt));  // open: gt, eq
  assign sltOut = {{31{1'b0}}, comparator_1_lt};  // Bit_Extender bit_extender_1
  Comparator #(.mode("unsigned"), .width(32)) comparator_2 (
    .a(dataA), .b(dataB), .lt(comparator_2_lt));  // open: gt, eq
  assign sltuOut = {{31{1'b0}}, comparator_2_lt};  // Bit_Extender bit_extender_2
  assign xorOut = dataA ^ dataB;  // XOR_Gate xor_1, 32 bits wide
  Shifter #(.shift("lr"), .width(32)) shifter_2 (.in(dataA), .\dist (dataB[4:0]), .out(srlOut));
  Shifter #(.shift("ar"), .width(32)) shifter_3 (.in(dataA), .\dist (dataB[4:0]), .out(sraOut));
  Multiplexer #(.select(4), .width(32)) multiplexer_1 (
    .in0(addOut), .in1(sllOut), .in2(sltOut), .in3(sltuOut), .in4(xorOut), .in5(srlOut), .in6(orOut),
    .in7(andOut), .in8(subOut), .in13(sraOut), .out(dataD), .sel(sel));  // open: in9, in10, in11, in12, in14, in15

  // Other names for the same wires on the sheet: dataA_t[31:0] = dataA; dataB_t[31:0] = dataB;
  //   dataBL5_t[4:0] = dataB[4:0]; dataD_t[31:0] = dataD; sel_t[3:0] = sel
endmodule

module RegisterFile (
  input  [4:0] rsi1,
  input  [4:0] rsi2,
  input  [4:0] rdi,
  input  [31:0] rd,
  input  we,
  input  clk,
  output [31:0] rs1,
  output [31:0] rs2
);

  wire r9we_t, x0we_t, x1we_t, x2we_t, x3we_t, x4we_t, x5we_t, x6we_t, x7we_t, x8we_t, x10we_t, x11we_t,
       x12we_t, x13we_t, x14we_t, x15we_t, x16we_t, x17we_t, x18we_t, x19we_t, x20we_t, x21we_t, x22we_t,
       x23we_t, x24we_t, x25we_t, x26we_t, x27we_t, x28we_t, x29we_t, x30we_t, x31we_t;
  wire [31:0] x1q_t, x2q_t, x3q_t, x4q_t, x5q_t, x6q_t, x7q_t, x8q_t, x9q_t, x10q_t, x11q_t, x12q_t, x13q_t,
       x14q_t, x15q_t, x16q_t, x17q_t, x18q_t, x19q_t, x20q_t, x21q_t, x22q_t, x23q_t, x24q_t, x25q_t,
       x26q_t, x27q_t, x28q_t, x29q_t, x30q_t, x31q_t;

  Demultiplexer #(.select(5)) demultiplexer_1 (
    .out0(x0we_t), .out1(x1we_t), .out2(x2we_t), .out3(x3we_t), .out4(x4we_t), .out5(x5we_t), .out6(x6we_t),
    .out7(x7we_t), .out8(x8we_t), .out9(r9we_t), .out10(x10we_t), .out11(x11we_t), .out12(x12we_t),
    .out13(x13we_t), .out14(x14we_t), .out15(x15we_t), .out16(x16we_t), .out17(x17we_t), .out18(x18we_t),
    .out19(x19we_t), .out20(x20we_t), .out21(x21we_t), .out22(x22we_t), .out23(x23we_t), .out24(x24we_t),
    .out25(x25we_t), .out26(x26we_t), .out27(x27we_t), .out28(x28we_t), .out29(x29we_t), .out30(x30we_t),
    .out31(x31we_t), .in(we), .sel(rdi));
  Register #(.width(32)) x4 (.D(rd), .en(x4we_t), .clk(clk), .Q(x4q_t));  // open: clr
  Register #(.width(32)) x8 (.D(rd), .en(x8we_t), .clk(clk), .Q(x8q_t));  // open: clr
  Register #(.width(32)) x12 (.D(rd), .en(x12we_t), .clk(clk), .Q(x12q_t));  // open: clr
  Register #(.width(32)) x16 (.D(rd), .en(x16we_t), .clk(clk), .Q(x16q_t));  // open: clr
  Register #(.width(32)) x20 (.D(rd), .en(x20we_t), .clk(clk), .Q(x20q_t));  // open: clr
  Register #(.width(32)) x24 (.D(rd), .en(x24we_t), .clk(clk), .Q(x24q_t));  // open: clr
  Register #(.width(32)) x28 (.D(rd), .en(x28we_t), .clk(clk), .Q(x28q_t));  // open: clr
  Register #(.width(32)) x1 (.D(rd), .en(x1we_t), .clk(clk), .Q(x1q_t));  // open: clr
  Register #(.width(32)) x5 (.D(rd), .en(x5we_t), .clk(clk), .Q(x5q_t));  // open: clr
  Register #(.width(32)) x9 (.D(rd), .en(r9we_t), .clk(clk), .Q(x9q_t));  // open: clr
  Register #(.width(32)) x13 (.D(rd), .en(x13we_t), .clk(clk), .Q(x13q_t));  // open: clr
  Register #(.width(32)) x17 (.D(rd), .en(x17we_t), .clk(clk), .Q(x17q_t));  // open: clr
  Register #(.width(32)) x21 (.D(rd), .en(x21we_t), .clk(clk), .Q(x21q_t));  // open: clr
  Register #(.width(32)) x25 (.D(rd), .en(x25we_t), .clk(clk), .Q(x25q_t));  // open: clr
  Register #(.width(32)) x29 (.D(rd), .en(x29we_t), .clk(clk), .Q(x29q_t));  // open: clr
  Register #(.width(32)) x2 (.D(rd), .en(x2we_t), .clk(clk), .Q(x2q_t));  // open: clr
  Register #(.width(32)) x6 (.D(rd), .en(x6we_t), .clk(clk), .Q(x6q_t));  // open: clr
  Register #(.width(32)) x10 (.D(rd), .en(x10we_t), .clk(clk), .Q(x10q_t));  // open: clr
  Register #(.width(32)) x14 (.D(rd), .en(x14we_t), .clk(clk), .Q(x14q_t));  // open: clr
  Register #(.width(32)) x18 (.D(rd), .en(x18we_t), .clk(clk), .Q(x18q_t));  // open: clr
  Register #(.width(32)) x22 (.D(rd), .en(x22we_t), .clk(clk), .Q(x22q_t));  // open: clr
  Register #(.width(32)) x26 (.D(rd), .en(x26we_t), .clk(clk), .Q(x26q_t));  // open: clr
  Register #(.width(32)) x30 (.D(rd), .en(x30we_t), .clk(clk), .Q(x30q_t));  // open: clr
  Register #(.width(32)) x3 (.D(rd), .en(x3we_t), .clk(clk), .Q(x3q_t));  // open: clr
  Register #(.width(32)) x7 (.D(rd), .en(x7we_t), .clk(clk), .Q(x7q_t));  // open: clr
  Register #(.width(32)) x11 (.D(rd), .en(x11we_t), .clk(clk), .Q(x11q_t));  // open: clr
  Register #(.width(32)) x15 (.D(rd), .en(x15we_t), .clk(clk), .Q(x15q_t));  // open: clr
  Register #(.width(32)) x19 (.D(rd), .en(x19we_t), .clk(clk), .Q(x19q_t));  // open: clr
  Register #(.width(32)) x23 (.D(rd), .en(x23we_t), .clk(clk), .Q(x23q_t));  // open: clr
  Register #(.width(32)) x27 (.D(rd), .en(x27we_t), .clk(clk), .Q(x27q_t));  // open: clr
  Register #(.width(32)) x31 (.D(rd), .en(x31we_t), .clk(clk), .Q(x31q_t));  // open: clr
  Multiplexer #(.select(5), .width(32)) multiplexer_1 (
    .in0({32{1'b0}}), .in1(x1q_t), .in2(x2q_t), .in3(x3q_t), .in4(x4q_t), .in5(x5q_t), .in6(x6q_t),
    .in7(x7q_t), .in8(x8q_t), .in9(x9q_t), .in10(x10q_t), .in11(x11q_t), .in12(x12q_t), .in13(x13q_t),
    .in14(x14q_t), .in15(x15q_t), .in16(x16q_t), .in17(x17q_t), .in18(x18q_t), .in19(x19q_t), .in20(x20q_t),
    .in21(x21q_t), .in22(x22q_t), .in23(x23q_t), .in24(x24q_t), .in25(x25q_t), .in26(x26q_t), .in27(x27q_t),
    .in28(x28q_t), .in29(x29q_t), .in30(x30q_t), .in31(x31q_t), .out(rs1), .sel(rsi1));
  Multiplexer #(.select(5), .width(32)) multiplexer_2 (
    .in0({32{1'b0}}), .in1(x1q_t), .in2(x2q_t), .in3(x3q_t), .in4(x4q_t), .in5(x5q_t), .in6(x6q_t),
    .in7(x7q_t), .in8(x8q_t), .in9(x9q_t), .in10(x10q_t), .in11(x11q_t), .in12(x12q_t), .in13(x13q_t),
    .in14(x14q_t), .in15(x15q_t), .in16(x16q_t), .in17(x17q_t), .in18(x18q_t), .in19(x19q_t), .in20(x20q_t),
    .in21(x21q_t), .in22(x22q_t), .in23(x23q_t), .in24(x24q_t), .in25(x25q_t), .in26(x26q_t), .in27(x27q_t),
    .in28(x28q_t), .in29(x29q_t), .in30(x30q_t), .in31(x31q_t), .out(rs2), .sel(rsi2));

  // Other names for the same wires on the sheet: clk_t = clk; rd_t[31:0] = rd; rdi_t[4:0] = rdi; rs1_t[31:0] = rs1;
  //   rs2_t[31:0] = rs2; rsi1_t[4:0] = rsi1; rsi2_t[4:0] = rsi2; we_t = we
endmodule

module Brancher (
  input  [31:0] dataA,
  input  [31:0] dataB,
  input  brUn,
  output brLt,
  output beEq
);

  wire comparator_1_lt, comparator_2_lt;

  Comparator #(.width(32)) comparator_1 (.a(dataA), .b(dataB), .eq(beEq), .lt(comparator_1_lt));  // open: gt
  Comparator #(.mode("unsigned"), .width(32)) comparator_2 (
    .a(dataA), .b(dataB), .lt(comparator_2_lt));  // open: gt, eq
  Multiplexer multiplexer_1 (.in0(comparator_1_lt), .in1(comparator_2_lt), .out(brLt), .sel(brUn));

  // Other names for the same wires on the sheet: brEq_t = beEq; brLt_t = brLt; brUn_t = brUn; dataA_t[31:0] = dataA;
  //   dataB_t[31:0] = dataB
endmodule

module SSplitter (
  input  [31:0] ins,
  output [6:0] opcode,
  output [4:0] imm4_0,
  output [2:0] funct3,
  output [4:0] rs1,
  output [4:0] rs2,
  output [6:0] imm11_5
);


  assign funct3 = ins[14:12];
  assign imm4_0 = ins[11:7];
  assign imm11_5 = ins[31:25];
  assign opcode = ins[6:0];
  assign rs1 = ins[19:15];
  assign rs2 = ins[24:20];
endmodule

module ISplitter (
  input  [31:0] ins,
  output [6:0] opcode,
  output [4:0] rd,
  output [2:0] funct3,
  output [4:0] rs1,
  output [11:0] imm11_0
);


  assign funct3 = ins[14:12];
  assign imm11_0 = ins[31:20];
  assign opcode = ins[6:0];
  assign rd = ins[11:7];
  assign rs1 = ins[19:15];
endmodule

module USplitter (
  input  [31:0] ins,
  output [6:0] opcode,
  output [4:0] rd,
  output [19:0] imm31_12
);


  assign imm31_12 = ins[31:12];
  assign opcode = ins[6:0];
  assign rd = ins[11:7];
endmodule

module BSplitter (
  input  [31:0] ins,
  output [6:0] opcode,
  output imm11,
  output [3:0] imm4_1,
  output [2:0] funct3,
  output [4:0] rs1,
  output [4:0] rs2,
  output [5:0] imm10_5,
  output imm12
);


  assign funct3 = ins[14:12];
  assign imm4_1 = ins[11:8];
  assign imm10_5 = ins[30:25];
  assign imm11 = ins[7];
  assign imm12 = ins[31];
  assign opcode = ins[6:0];
  assign rs1 = ins[19:15];
  assign rs2 = ins[24:20];
endmodule

module JSplitter (
  input  [31:0] ins,
  output [6:0] opcode,
  output [4:0] rd,
  output [7:0] imm19_12,
  output imm11,
  output [9:0] imm10_1,
  output imm20
);


  assign imm10_1 = ins[30:21];
  assign imm11 = ins[20];
  assign imm19_12 = ins[19:12];
  assign imm20 = ins[31];
  assign opcode = ins[6:0];
  assign rd = ins[11:7];
endmodule

module RSplitter (
  input  [31:0] ins,
  output [6:0] opcode,
  output [4:0] rd,
  output [2:0] funct3,
  output [4:0] rs1,
  output [4:0] rs2,
  output [6:0] funct7
);


  assign funct3 = ins[14:12];
  assign funct7 = ins[31:25];
  assign opcode = ins[6:0];
  assign rd = ins[11:7];
  assign rs1 = ins[19:15];
  assign rs2 = ins[24:20];
endmodule

module ControlLogic (
  input  [31:0] ins,
  output [3:0] alusel,
  output regwena,
  output [2:0] immsel,
  output bsel
);

  ROM #(.addrWidth(9), .dataWidth(9)) rom_1 (
    .addr({ins[30], ins[14:12], ins[6:2]}), .data({alusel, regwena, immsel, bsel}));

  // Other names for the same wires on the sheet: i2_t = ins[2]; i3_t = ins[3]; i4_t = ins[4]; i5_t = ins[5];
  //   i6_t = ins[6]; i12_t = ins[12]; i13_t = ins[13]; i14_t = ins[14]; i30_t = ins[30]; bsel_t = bsel;
  //   regwena_t = regwena; as0_t = alusel[0]; as1_t = alusel[1]; as2_t = alusel[2]; as3_t = alusel[3];
  //   immsel0_t = immsel[0]; immsel1_t = immsel[1]; immsel2_t = immsel[2]

  // Notes on the sheet:
  //   contents of rom_1 (hex, n*v repeats v):
  //   4*0 11 7*0 10 23*0 31 7*0 30 23*0 51 7*0 50 23*0 71 7*0 70 23*0 91 7*0 90 23*0 b1 7*0 b0 23*0 d1 7*0
  //   d0 23*0 f1 7*0 f0 31*0 110 151*0 1b1 7*0 1b0
endmodule

module ALUctl (
  input  [31:0] rs2,
  input  [31:0] imm31_0,
  input  bsel,
  output [31:0] dataB
);

  Multiplexer #(.width(32)) multiplexer_1 (.in0(rs2), .in1(imm31_0), .out(dataB), .sel(bsel));
endmodule

module immediateGenerator (
  input  [31:0] ins,
  input  [2:0] sel,
  output [31:0] imm31_0
);

  wire [3:0] bsplitter_1_imm4_1;
  wire [4:0] ssplitter_1_imm4_0;
  wire [5:0] bsplitter_1_imm10_5;
  wire [6:0] ssplitter_1_imm11_5;
  wire [7:0] jsplitter_1_imm19_12;
  wire [9:0] jsplitter_1_imm10_1;
  wire [11:0] isplitter_1_imm11_0;
  wire [12:11] bsplitter_1_imm11;
  wire [20:11] jsplitter_1_imm11;
  wire [31:0] BOut_t, IOut_t, JOut_t, SOut_t;
  wire [31:12] UOut_t;

  ISplitter isplitter_1 (.ins(ins), .imm11_0(isplitter_1_imm11_0));  // open: opcode, rd, funct3, rs1
  SSplitter ssplitter_1 (
    .ins(ins), .imm4_0(ssplitter_1_imm4_0), .imm11_5(ssplitter_1_imm11_5));  // open: opcode, funct3, rs1, rs2
  BSplitter bsplitter_1 (
    .ins(ins), .imm11(bsplitter_1_imm11[11]), .imm4_1(bsplitter_1_imm4_1), .imm10_5(bsplitter_1_imm10_5),
    .imm12(bsplitter_1_imm11[12]));  // open: opcode, funct3, rs1, rs2
  JSplitter jsplitter_1 (
    .ins(ins), .imm19_12(jsplitter_1_imm19_12), .imm11(jsplitter_1_imm11[11]), .imm10_1(jsplitter_1_imm10_1),
    .imm20(jsplitter_1_imm11[20]));  // open: opcode, rd
  USplitter usplitter_1 (.ins(ins), .imm31_12(UOut_t));  // open: opcode, rd
  assign IOut_t = {{20{isplitter_1_imm11_0[11]}}, isplitter_1_imm11_0};  // Bit_Extender bit_extender_1
  assign SOut_t = {{20{ssplitter_1_imm11_5[6]}}, {ssplitter_1_imm11_5, ssplitter_1_imm4_0}};  // Bit_Extender bit_extender_2
  assign BOut_t = {{19{bsplitter_1_imm11[12]}}, {bsplitter_1_imm11, bsplitter_1_imm10_5, bsplitter_1_imm4_1, 1'b0}};  // Bit_Extender bit_extender_3
  assign JOut_t = {{11{jsplitter_1_imm11[20]}}, {jsplitter_1_imm11[20], jsplitter_1_imm19_12, jsplitter_1_imm11[11], jsplitter_1_imm10_1, 1'b0}};  // Bit_Extender bit_extender_4
  Multiplexer #(.select(3), .width(32)) multiplexer_1 (
    .in0(IOut_t), .in1(SOut_t), .in2(BOut_t), .in3(JOut_t), .in4({UOut_t, {12{1'b0}}}), .out(imm31_0),
    .sel(sel));  // open: in5, in6, in7

  // Other names for the same wires on the sheet: imm31_0_t[31:0] = imm31_0; ins_t[31:0] = ins; sel_t[2:0] = sel
endmodule

module LoadByte (
  input  [31:0] A,
  input  [31:0] Lw,
  output [31:0] Lb,
  output [31:0] Lbu
);

  wire [4:0] bitselector_1_out;
  wire [7:0] bitselector_2_out;
  wire [31:0] and_1_out, shifter_1_out, shifter_2_out, subtractor_1_out;

  assign and_1_out = A & 32'h3;  // AND_Gate and_1, 32 bits wide
  Subtractor #(.width(32)) subtractor_1 (.a(32'h3), .b(and_1_out), .out(subtractor_1_out));  // open: bin, bout
  Shifter #(.width(32)) shifter_1 (.in(subtractor_1_out), .\dist (5'b00011), .out(shifter_1_out));
  BitSelector #(.group(5), .width(32)) bitselector_1 (.in(shifter_1_out), .out(bitselector_1_out), .sel(3'b000));
  Shifter #(.shift("lr"), .width(32)) shifter_2 (.in(Lw), .\dist (bitselector_1_out), .out(shifter_2_out));
  assign Lbu = 32'hff & shifter_2_out;  // AND_Gate and_2, 32 bits wide
  BitSelector #(.group(8), .width(32)) bitselector_2 (.in(shifter_2_out), .out(bitselector_2_out), .sel(2'b00));
  assign Lb = {{24{bitselector_2_out[7]}}, bitselector_2_out};  // Bit_Extender bit_extender_1

  // Other names for the same wires on the sheet: A_t[31:0] = A; Ib_t[31:0] = Lb; Iw_t[31:0] = Lw; lbu_t[31:0] = Lbu
endmodule

module LoadHalfWord (
  input  [31:0] A,
  input  [31:0] Lw,
  output [31:0] Lh,
  output [31:0] Lhu
);

  wire bitselector_1_out, not_1_out;
  wire [15:0] bitselector_2_out;

  BitSelector #(.width(32)) bitselector_1 (.in(A), .out(bitselector_1_out), .sel(5'b00001));
  not not_1 (not_1_out, bitselector_1_out);
  BitSelector #(.group(16), .width(32)) bitselector_2 (.in(Lw), .out(bitselector_2_out), .sel(not_1_out));
  assign Lh = {{16{bitselector_2_out[15]}}, bitselector_2_out};  // Bit_Extender bit_extender_1
  assign Lhu = {{16{1'b0}}, bitselector_2_out};  // Bit_Extender bit_extender_2

  // Other names for the same wires on the sheet: A_t[31:0] = A; Ih_t[31:0] = Lh; Ihu_t[31:0] = Lhu; Iw_t[31:0] = Lw
endmodule

module LoadCtr (
  output [31:0] out_1
);

  wire [31:0] loadbyte_1_lb, loadbyte_1_lbu, loadhalfword_1_lh, loadhalfword_1_lhu, multiplexer_1_out;

  LoadByte loadbyte_1 (.A({32{1'b0}}), .Lw(32'h81223344), .Lb(loadbyte_1_lb), .Lbu(loadbyte_1_lbu));
  LoadHalfWord loadhalfword_1 (.A({32{1'b0}}), .Lw(32'h81223344), .Lh(loadhalfword_1_lh), .Lhu(loadhalfword_1_lhu));
  Multiplexer #(.select(3), .width(32)) multiplexer_1 (
    .in0(loadbyte_1_lb), .in1(loadhalfword_1_lh), .in2(32'h81223344), .in4(loadbyte_1_lbu),
    .in5(loadhalfword_1_lhu), .out(multiplexer_1_out), .sel(3'b101));  // open: in3, in6, in7
  Multiplexer #(.width(32)) multiplexer_2 (.in0(multiplexer_1_out), .in1({32{1'b0}}), .out(out_1), .sel(1'b0));

  // Other names for the same wires on the sheet: D_t[31:0] = out_1
endmodule
