// Logisim project Program_Counter.circ as structural Verilog: 1 circuit, main circuit main
module main (
  input  [31:0] inPC,
  input  clk,
  output [31:0] outPCPlus4,
  output [31:0] outPC
);

  Register #(.width(32)) register_1 (.D(inPC), .en(1'b1), .clk(clk), .Q(outPC));  // open: clr
  Adder #(.width(32)) adder_1 (.a(outPC), .b(32'h4), .out(outPCPlus4));  // open: cin, cout

  // Other names for the same wires on the sheet: clk_t = clk; inPC_t[31:0] = inPC; outPC_t[31:0] = outPC;
  //   outPCPlus4_t[31:0] = outPCPlus4
endmodule
