// Logisim project immediate_gen.circ as structural Verilog
module main (
  input  [31:0] ins,
  input  [2:0] sel,
  output [31:0] imm31_0
);

  wire [3:0] bsplitter_1_imm4_1;
  wire [4:0] ssplitter_1_imm4_0;
  wire [5:0] bsplitter_1_imm10_5;
  wire [6:0] ssplitter_1_imm11_5;
  wire [7:0] jsplitter_1_imm19_12;
  wire [9:0] jsplitter_1_imm10_1;
  wire [11:0] isplitter_1_imm11_0;
  wire [12:11] bsplitter_1_imm11;
  wire [20:11] jsplitter_1_imm11;
  wire [31:0] BOut_t, IOut_t, JOut_t, SOut_t;
  wire [31:12] UOut_t;

  ISplitter isplitter_1 (.ins(ins), .imm11_0(isplitter_1_imm11_0));  // open: opcode, rd, funct3, rs1
  SSplitter ssplitter_1 (
    .ins(ins), .imm4_0(ssplitter_1_imm4_0), .imm11_5(ssplitter_1_imm11_5));  // open: opcode, funct3, rs1, rs2
  BSplitter bsplitter_1 (
    .ins(ins), .imm11(bsplitter_1_imm11[11]), .imm4_1(bsplitter_1_imm4_1), .imm10_5(bsplitter_1_imm10_5),
    .imm12(bsplitter_1_imm11[12]));  // open: opcode, funct3, rs1, rs2
  JSplitter jsplitter_1 (
    .ins(ins), .imm19_12(jsplitter_1_imm19_12), .imm11(jsplitter_1_imm11[11]), .imm10_1(jsplitter_1_imm10_1),
    .imm20(jsplitter_1_imm11[20]));  // open: opcode, rd
  USplitter usplitter_1 (.ins(ins), .imm31_12(UOut_t));  // open: opcode, rd
  assign IOut_t = {{20{isplitter_1_imm11_0[11]}}, isplitter_1_imm11_0};  // Bit_Extender bit_extender_1
  assign SOut_t = {{20{ssplitter_1_imm11_5[6]}}, {ssplitter_1_imm11_5, ssplitter_1_imm4_0}};  // Bit_Extender bit_extender_2
  assign BOut_t = {{19{bsplitter_1_imm11[12]}}, {bsplitter_1_imm11, bsplitter_1_imm10_5, bsplitter_1_imm4_1, 1'b0}};  // Bit_Extender bit_extender_3
  assign JOut_t = {{11{jsplitter_1_imm11[20]}}, {jsplitter_1_imm11[20], jsplitter_1_imm19_12, jsplitter_1_imm11[11], jsplitter_1_imm10_1, 1'b0}};  // Bit_Extender bit_extender_4
  Multiplexer #(.select(3), .width(32)) multiplexer_1 (
    .in0(IOut_t), .in1(SOut_t), .in2(BOut_t), .in3(JOut_t), .in4({UOut_t, {12{1'b0}}}), .out(imm31_0),
    .sel(sel));  // open: in5, in6, in7

  // Other names for the same wires on the sheet: imm31_0_t[31:0] = imm31_0; ins_t[31:0] = ins; sel_t[2:0] = sel
endmodule

module SSplitter (
  input  [31:0] ins,
  output [6:0] opcode,
  output [4:0] imm4_0,
  output [2:0] funct3,
  output [4:0] rs1,
  output [4:0] rs2,
  output [6:0] imm11_5
);


  assign funct3 = ins[14:12];
  assign imm4_0 = ins[11:7];
  assign imm11_5 = ins[31:25];
  assign opcode = ins[6:0];
  assign rs1 = ins[19:15];
  assign rs2 = ins[24:20];
endmodule

module ISplitter (
  input  [31:0] ins,
  output [6:0] opcode,
  output [4:0] rd,
  output [2:0] funct3,
  output [4:0] rs1,
  output [11:0] imm11_0
);


  assign funct3 = ins[14:12];
  assign imm11_0 = ins[31:20];
  assign opcode = ins[6:0];
  assign rd = ins[11:7];
  assign rs1 = ins[19:15];
endmodule

module USplitter (
  input  [31:0] ins,
  output [6:0] opcode,
  output [4:0] rd,
  output [19:0] imm31_12
);


  assign imm31_12 = ins[31:12];
  assign opcode = ins[6:0];
  assign rd = ins[11:7];
endmodule

module BSplitter (
  input  [31:0] ins,
  output [6:0] opcode,
  output imm11,
  output [3:0] imm4_1,
  output [2:0] funct3,
  output [4:0] rs1,
  output [4:0] rs2,
  output [5:0] imm10_5,
  output imm12
);


  assign funct3 = ins[14:12];
  assign imm4_1 = ins[11:8];
  assign imm10_5 = ins[30:25];
  assign imm11 = ins[7];
  assign imm12 = ins[31];
  assign opcode = ins[6:0];
  assign rs1 = ins[19:15];
  assign rs2 = ins[24:20];
endmodule

module JSplitter (
  input  [31:0] ins,
  output [6:0] opcode,
  output [4:0] rd,
  output [7:0] imm19_12,
  output imm11,
  output [9:0] imm10_1,
  output imm20
);


  assign imm10_1 = ins[30:21];
  assign imm11 = ins[20];
  assign imm19_12 = ins[19:12];
  assign imm20 = ins[31];
  assign opcode = ins[6:0];
  assign rd = ins[11:7];
endmodule
